// Logisim project 7 segment - display - Logisim.circ as structural Verilog: 1 circuit, main circuit main
module main (
  input  D,
  input  C,
  input  B,
  input  A
);

  wire A_out, and_1_out, and_2_out, and_3_out, and_4_out, and_5_out, and_6_out, and_7_out, and_8_out,
       and_9_out, and_10_out, and_11_out, and_12_out, and_13_out, and_14_out, and_15_out, and_16_out, B_out,
       C_out, D_out, E_out, F_out, not_1_out, not_2_out, not_3_out, not_4_out, not_5_out, not_6_out,
       not_7_out, not_8_out, not_9_out, not_10_out, not_11_out, not_12_out, not_13_out, not_14_out,
       not_15_out, not_16_out, not_17_out, not_18_out, not_19_out, not_20_out, not_21_out, or_1_out;

  not not_1 (not_1_out, D);
  not not_2 (not_2_out, B);
  not not_3 (not_3_out, D);
  not not_4 (not_4_out, C);
  not not_5 (not_5_out, B);
  not not_6 (not_6_out, D);
  not not_7 (not_7_out, B);
  not not_8 (not_8_out, D);
  not not_9 (not_9_out, C);
  not not_10 (not_10_out, B);
  not not_11 (not_11_out, D);
  not not_12 (not_12_out, D);
  not not_13 (not_13_out, C);
  not not_14 (not_14_out, D);
  not not_15 (not_15_out, C);
  not not_16 (not_16_out, D);
  not not_17 (not_17_out, C);
  not not_18 (not_18_out, D);
  not not_19 (not_19_out, B);
  and and_1 (and_1_out, not_1_out, not_2_out);
  and and_2 (and_2_out, D, B);
  and and_3 (and_3_out, D, C);
  and and_4 (and_4_out, not_3_out, not_4_out);
  and and_5 (and_5_out, not_5_out, not_6_out);
  and and_6 (and_6_out, not_7_out, C);
  and and_7 (and_7_out, C, not_8_out);
  and and_8 (and_8_out, B, not_9_out, D);
  and and_9 (and_9_out, not_10_out, not_11_out);
  and and_10 (and_10_out, C, not_12_out);
  and and_11 (and_11_out, not_13_out, not_14_out);
  and and_12 (and_12_out, B, not_15_out);
  and and_13 (and_13_out, not_16_out, B);
  and and_14 (and_14_out, not_17_out, B);
  and and_15 (and_15_out, not_18_out, B);
  and and_16 (and_16_out, not_19_out, C);
  not not_20 (not_20_out, B);
  not not_21 (not_21_out, C);
  or u_C (C_out, D, not_21_out, B);
  or E (E_out, and_9_out, and_10_out);
  or u_A (A_out, and_1_out, and_2_out, C, A);
  or u_B (B_out, and_3_out, not_20_out, and_4_out);
  or F (F_out, A, and_11_out, and_12_out, and_13_out);
  or or_1 (or_1_out, and_14_out, A, and_15_out, and_16_out);
  or u_D (D_out, and_5_out, A, and_6_out, and_7_out, and_8_out);
  _7_Segment_Display u_7_segment_display_1 (
    .g(or_1_out), .f(F_out), .a(A_out), .b(B_out), .e(E_out), .d(D_out), .c(C_out));  // open: dp
endmodule
